// Logisim project 11vaja.circ as structural Verilog: 3 circuits, main circuit main
module main (
  input  x1,
  output y1,
  output y2
);

  wire clock_1_out, not_1_out, not_2_out, q1_q, q2_q, t1_1_out_4, t2_1_out_4;

  t1 t1_1 (.q1(q1_q), .q2(q2_q), .x(x1), .out_4(t1_1_out_4));
  t2 t2_1 (.q1(q1_q), .q2(q2_q), .x(x1), .out_4(t2_1_out_4));
  Clock clock_1 (.out(clock_1_out));
  T_Flip_Flop q1 (.T(t1_1_out_4), .clk(clock_1_out), .Q(q1_q));  // open: Qn, reset, preset
  T_Flip_Flop q2 (.T(t2_1_out_4), .clk(clock_1_out), .Q(q2_q));  // open: Qn, reset, preset
  not not_1 (not_1_out, q2_q);
  not not_2 (not_2_out, q1_q);
  and and_1 (y1, q1_q, not_1_out);
  and and_2 (y2, not_2_out, q2_q);
endmodule

module t1 (
  input  q1,
  input  q2,
  input  x,
  output out_4
);

  wire and_1_out, and_2_out, and_3_out, not_1_out, not_2_out, not_3_out;

  not not_1 (not_1_out, x);
  not not_2 (not_2_out, q1);
  not not_3 (not_3_out, q2);
  and and_1 (and_1_out, q1, q2);
  and and_2 (and_2_out, q1, not_1_out);
  and and_3 (and_3_out, not_2_out, not_3_out);
  or or_1 (out_4, and_1_out, and_2_out, and_3_out);
endmodule

module t2 (
  input  q1,
  input  q2,
  input  x,
  output out_4
);

  wire and_1_out, and_2_out, and_3_out, not_1_out, not_2_out, not_3_out;

  not not_1 (not_1_out, x);
  not not_2 (not_2_out, x);
  not not_3 (not_3_out, q2);
  and and_1 (and_1_out, q1, not_1_out);
  and and_2 (and_2_out, q2, not_2_out);
  and and_3 (and_3_out, x, not_3_out);
  or or_1 (out_4, and_1_out, and_2_out, and_3_out);
endmodule
